# Fritzing sketch TUBES (saved by Fritzing 0.9.5d)
breadboards: 1

parts:
  Raspberry_Pi_1 = Raspberry Pi 3 [part_number=RPI-3-V1.2]  # not connected
  Part1 = Arduino Uno (Rev3)
  RHT1 = Humidity and Temperature Sensor RHT03
  Part2 = Soil Moisture Sensor

nets:
  N1: Part1.A0, Part2.SIG
  N2: Part1.D8, RHT1.Data-signal
  VCC: Part1.3V3, RHT1.Vcc, Part2.VCC
  GND: Part1.GND, RHT1.GND_2, Part2.GND

notes:
  Arduino dihubungkan ke RPI melalui port USB
